# Fritzing sketch furnace-remote-listener (saved by Fritzing 1.0.6)
breadboards: 1

parts:
  Part1 = Arduino Nano (Rev3.0) (ICSP)
  YwRobot_Power_Supply1 = YwRobot Breadboard Power Supply [part_number=545043]
  Part3 = NRF24L01+ Breakout Board
  C1 = Capacitor Polarized [package=panasonic_c]
  Part4 = Adafruit MAX4466 Electret Microphone Amplifier [part_number="Adafruit #1063"]
  C2 = Ceramic Capacitor [capacitance=100nF voltage=35V package="100 mil [THT, multilayer]"]
  C3 = Ceramic Capacitor [capacitance=100nF voltage=35V package="100 mil [THT, multilayer]"]
  C4 = Electrolytic Capacitor [capacitance=1µF voltage=35V package="100 mil [THT, electrolytic]"]

nets:
  GND: Part1.GND, YwRobot_Power_Supply1.GND#13, YwRobot_Power_Supply1.GND#14, Part3.GND, C1.-, Part4.GND, C2.1, C3.1, C4.-
  N1: Part1.D9, Part3.CE
  N2: Part1.D10, Part3.CS
  N3: Part1.D11/MOSI, Part3.MOSI
  N4: Part1.D12/MISO, Part3.MISO
  5V: Part1.5V, YwRobot_Power_Supply1.VCC#9, YwRobot_Power_Supply1.VCC#10, Part4.VCC, C2.0, C4.+
  N5: Part1.A0, Part4.OUT, C3.0
  3V3: Part1.3V3, Part3.VCC, C1.+
  N6: Part1.D13/SCK, Part3.SCK
  N7: YwRobot_Power_Supply1.VCC#5, YwRobot_Power_Supply1.VCC#6
  N8: YwRobot_Power_Supply1.GND#11, YwRobot_Power_Supply1.GND#12

notes:
  100 µF electrolytic
  As close as possible to nRF24 VCC/GND
  10 µF electrolytic for bulk supply smoothing
  0.1 µF ceramic for supply decoupling
  0.1 µF ceramic for output noise filtering
  Radio REQUIRES clean 3.3v from Arduino
  Signals:
  CE → D9, CSN → D10
  MOSI/MISO/SCK on D11/D12/D13 (SPI bus)

custom parts:
  YwRobot Breadboard Power Supply: The YwRobot Breadboard Power Supply (MB-V2) has two power rails; they can be 5V or 3V3. Power to the module can be provided through the female USB socket or through the A10 (female) 2.1mm power jack.
  Adafruit MAX4466 Electret Microphone Amplifier: Add an ear to your project with this well-designed electret microphone amplifier. This fully assembled and tested board comes with a 20-20KHz electret microphone soldered on. For the amplification, we use the Maxim MAX4466, an op-amp specifically designed for this delicate task! The amplifier has excellent power supply noise rejection, so this amplifier sounds really good and isn't nearly as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
